// Logisim project Atividade 1.circ as structural Verilog: 1 circuit, main circuit main
module main (
  input  A,
  input  B,
  input  C,
  input  D,
  input  E,
  input  F
);

  wire and_1_out, and_2_out, and_3_out, or_1_out;

  and and_1 (and_1_out, A, B);
  and and_2 (and_2_out, C, D);
  and and_3 (and_3_out, E, F);
  or or_1 (or_1_out, and_1_out, and_2_out);
  // OR_Gate or_2 has open pins: in1=or_1_out, in3=and_3_out, out=open

  // Notes on the sheet:
  //   S
endmodule
